// Digital circuit flags.dig as structural Verilog
module flags (
  input  isCmp,
  input  is_gt,
  input  is_eq,
  output flags_GT,
  output flags_E
);

  D_FF d_ff_1 (.D(is_gt), .C(isCmp), .Q(flags_GT));  // open: nQ
  D_FF d_ff_2 (.D(is_eq), .C(isCmp), .Q(flags_E));  // open: nQ
endmodule
