// Digital circuit processor.dig as structural Verilog
module processor (
  input  clk
);

  wire add_1_s, add_2_s, branch_tgt, control_unit_1_isbeq, control_unit_1_isbgt, control_unit_1_iscall,
       control_unit_1_isld, control_unit_1_isubranch, control_unit_1_iswb, data_lck_1_datalockconflict,
       ex_ma_1_iscall_o, ex_ma_1_isld_o, ex_ma_1_isst_o, ex_ma_1_iswb_o, isBranchTaken, isRet, isSt, isWb,
       multiplexer_5_out, of_ex_1_p1, of_ex_1_p11, RW__gt_EX_op2, RW__gt_MA_op2, RW__gt_OF_op1,
       RW__gt_OF_op2, RW_MA_op1, RW_MA_op2, stall, undriven_4, undriven_5, undriven_6, undriven_7;
  wire [1:0] ma_rw_1_isld_o;
  wire [3:0] if_of_1_inst_out_2, multiplexer_3_out, multiplexer_4_out, \reg ;
  wire [12:0] control_unit_1_sinalula;
  wire [17:0] if_of_1_inst_out;
  wire [23:0] PC_q_2;
  wire [26:22] if_of_1_inst_out_3;
  wire [31:0] add_3_s, barrelshifter_1_out, bitextender_1_out, data, ex_ma_1_alur_out, ex_ma_1_instr_out,
       ex_ma_1_op2_out, ex_ma_1_pc_out, EX_MA_Instruction, if_of_1_pc_out, IF_OF_Instruction,
       ma_rw_1_alur_out, ma_rw_1_instr_out, ma_rw_1_loadr_out, ma_rw_1_pc_out, MA_RW_Instruction,
       memory_unit_1_idresult, multiplexer_1_out, multiplexer_2_out, multiplexer_6_out, multiplexer_7_out,
       multiplexer_8_out, OF_EX_Instruction, PC_q, registerfile_1_da, registerfile_1_db, rom_1_d, undriven,
       undriven_2, undriven_3;
  wire [31:1] undriven_8;
  wire [31:27] if_of_1_inst_out_4;

  Multiplexer multiplexer_1 (.sel(isBranchTaken), .in_0(add_1_s), .in_1(branch_tgt), .out(multiplexer_1_out[0]));
  Register #(.Bits(32)) PC (.D(multiplexer_1_out), .C(clk), .en(1'b1), .Q({PC_q[31:26], PC_q_2, PC_q[1:0]}));
  Add add_1 (.a(PC_q[0]), .b(1'b0), .c_i(1'b0), .s(add_1_s));  // open: c_o
  Data_Lck data_lck_1 (
    .IF_OF(IF_OF_Instruction), .OF_EX(OF_EX_Instruction), .DataLockConflict(data_lck_1_datalockconflict));
  // forwarding_unit forwarding_unit_1: pin names not known; wires that end beside it: MA_RW_Instruction, EX_MA_Instruction, OF_EX_Instruction, IF_OF_Instruction, RW__gt_MA_op2, RW__gt_OF_op2, RW__gt_OF_op1, RW_MA_op2, RW_MA_op1, RW__gt_EX_op2
  ROM #(.AddrBits(20), .Bits(32)) rom_1 (.A(PC_q_2[19:0]), .sel(1'b1), .D(rom_1_d));
  not not_1 (stall, data_lck_1_datalockconflict);
  Multiplexer #(.Bits(32)) multiplexer_2 (
    .sel(isBranchTaken), .in_0(rom_1_d), .in_1(32'h68000000), .out(multiplexer_2_out));
  IF_OF if_of_1 (
    .stall(stall), .PC({PC_q[31:26], PC_q_2, PC_q[1:0]}), .Inst(multiplexer_2_out), .clkIn(clk),
    .bubble(IF_OF_Instruction), .Pc_out(if_of_1_pc_out),
    .Inst_out({if_of_1_inst_out_4, if_of_1_inst_out_3, if_of_1_inst_out_2, if_of_1_inst_out}));
  control_unit control_unit_1 (
    .opcode(if_of_1_pc_out[31:27]), .I_bit(if_of_1_pc_out[26]), .isSt(isSt), .isLd(control_unit_1_isld),
    .isBeq(control_unit_1_isbeq), .isBgt(control_unit_1_isbgt), .isRet(isRet), .isWb(control_unit_1_iswb),
    .isUbranch(control_unit_1_isubranch), .isCall(control_unit_1_iscall), .SinalULA(control_unit_1_sinalula));  // open: isImm
  Multiplexer #(.Bits(4)) multiplexer_3 (
    .sel(isRet), .in_0(if_of_1_inst_out_2), .in_1(4'b1111), .out(multiplexer_3_out));
  Multiplexer #(.Bits(4)) multiplexer_4 (
    .sel(isSt), .in_0(if_of_1_inst_out[17:14]), .in_1(if_of_1_inst_out_3[25:22]), .out(multiplexer_4_out));
  BitExtender #(.inputBits(27), .outputBits(32)) bitextender_1 (
    .in({if_of_1_inst_out_3, if_of_1_inst_out_2, if_of_1_inst_out}), .out(bitextender_1_out));
  calculate_immediate calculate_immediate_1 (.imm(if_of_1_inst_out));  // open: imm_x
  BarrelShifter #(.Bits(32)) barrelshifter_1 (.in(bitextender_1_out), .shift(5'b00010), .out(barrelshifter_1_out));
  RegisterFile registerfile_1 (
    .Din(data[0]), .we(isWb), .Rw(\reg [1:0]), .C(clk), .Ra(multiplexer_4_out[1:0]),
    .Rb(multiplexer_3_out[1:0]), .Da(registerfile_1_da[0]), .Db(registerfile_1_db[0]));
  Multiplexer multiplexer_5 (.in_0(multiplexer_7_out[0]), .in_1(of_ex_1_p1), .out(multiplexer_5_out));  // open: sel
  Add add_2 (.a(barrelshifter_1_out[0]), .b(if_of_1_pc_out[0]), .c_i(1'b0), .s(add_2_s));  // open: c_o
  Multiplexer #(.Bits(32)) multiplexer_6 (
    .sel(RW__gt_OF_op1), .in_0(registerfile_1_da), .in_1(data), .out(multiplexer_6_out));
  Multiplexer #(.Bits(32)) multiplexer_7 (
    .sel(RW__gt_OF_op2), .in_0(registerfile_1_db), .in_1(data), .out(multiplexer_7_out));
  // OF_EX of_ex_1: pin names not known; wires that end beside it: of_ex_1_p1, isSt, control_unit_1_iscall, control_unit_1_iswb, {if_of_1_inst_out_4, if_of_1_inst_out_3, if_of_1_inst_out_2, if_of_1_inst_out}, if_of_1_pc_out, add_2_s, multiplexer_5_out, multiplexer_6_out, multiplexer_7_out, of_ex_1_p11, clk
  or or_1 (of_ex_1_p11, ~stall, isBranchTaken);  // Or
  EX_MA ex_ma_1 (
    .PC(undriven), .op2(undriven_2), .instr(undriven_3), .isld(undriven_4), .isst(undriven_5),
    .iscall(undriven_6), .iswb(undriven_7), .clkIn(clk), .instr_out2(EX_MA_Instruction),
    .PC_out(ex_ma_1_pc_out), .aluR_out(ex_ma_1_alur_out), .op2_out(ex_ma_1_op2_out),
    .instr_out(ex_ma_1_instr_out), .iswb_o(ex_ma_1_iswb_o), .iscall_o(ex_ma_1_iscall_o),
    .isst_o(ex_ma_1_isst_o), .isld_o(ex_ma_1_isld_o));  // open: aluR
  Multiplexer #(.Bits(32)) multiplexer_8 (
    .sel(RW__gt_MA_op2), .in_0(ex_ma_1_op2_out), .in_1(data), .out(multiplexer_8_out));
  Memory_Unit memory_unit_1 (
    .MAR(ex_ma_1_alur_out), .MDR(multiplexer_8_out), .isSt(ex_ma_1_isst_o), .isLd(ex_ma_1_isld_o), .Clk(clk),
    .IdResult(memory_unit_1_idresult));
  MA_RW ma_rw_1 (
    .PC(ex_ma_1_pc_out), .loadR(memory_unit_1_idresult), .aluR(ex_ma_1_alur_out), .instr(ex_ma_1_instr_out),
    .isld(ex_ma_1_isld_o), .iscall(ex_ma_1_iscall_o), .iswb(ex_ma_1_iswb_o), .clkIn(clk),
    .instr_out2(MA_RW_Instruction), .PC_out(ma_rw_1_pc_out), .loadR_out(ma_rw_1_loadr_out),
    .aluR_out(ma_rw_1_alur_out), .instr_out(ma_rw_1_instr_out), .iswb_o(isWb), .iscall_o(ma_rw_1_isld_o[1]),
    .isld_o(ma_rw_1_isld_o[0]));
  Multiplexer #(.Bits(4)) multiplexer_9 (
    .sel(ma_rw_1_isld_o[1]), .in_0(ma_rw_1_instr_out[25:22]), .in_1(4'b1111), .out(\reg ));
  Add #(.Bits(32)) add_3 (.a(ma_rw_1_pc_out), .b(32'h4), .c_i(1'b0), .s(add_3_s));  // open: c_o
  Multiplexer #(.Bits(32), .Selector_Bits(2)) multiplexer_10 (
    .sel(ma_rw_1_isld_o), .in_0(ma_rw_1_alur_out), .in_1(ma_rw_1_loadr_out), .in_2(add_3_s),
    .in_3({undriven_8, 1'b0}), .out(data));
  // Pins of 1 and 32 bits meet at {PC_q[31:26], PC_q_2, PC_q[1:0]}
  // Pins of 1 and 32 bits meet at if_of_1_pc_out
  // Pins of 20 and 24 bits meet at PC_q_2
  // Pins of 1 and 32 bits meet at multiplexer_1_out
  // Pins of 1 and 32 bits meet at 32'h4
  // Pins of 1 and 32 bits meet at {32{1'b0}}
  // Pins of 1 and 32 bits meet at data
  // Pins of 2 and 4 bits meet at \reg 
  // Pins of 2 and 4 bits meet at multiplexer_4_out
  // Pins of 2 and 4 bits meet at multiplexer_3_out
  // Pins of 1 and 32 bits meet at registerfile_1_da
  // Pins of 1 and 32 bits meet at registerfile_1_db
endmodule
