// Digital circuit ula.dig as structural Verilog
module ula (
  input  [31:0] B,
  input  [31:0] A,
  input  [3:0] ALU_signals,
  output is_gt,
  output is_eq,
  output [31:0] aluResult
);

  wire [31:0] in_0, in_1, in_2, in_3, in_4, in_6, in_7, in_8, in_9, in_10, in_11;
  wire [63:32] mult_mul;

  assign in_10 = A & B;  // And and_1, 32 bits wide
  assign in_11 = A | B;  // Or or_1, 32 bits wide
  Add #(.Bits(32)) add (.a(A), .b(B), .c_i(1'b0), .s(in_0));  // open: c_o
  Sub #(.Bits(32)) sub (.a(A), .b(B), .c_i(1'b0), .s(in_1));  // open: c_o
  Mul #(.Bits(32)) mult (.a(A), .b(B), .mul({mult_mul, in_2}));
  Div #(.Bits(32)) div (.a(A), .b(B), .q(in_3), .r(in_4));
  Comparator #(.Bits(32)) comp (.a(A), .b(B), .gt(is_gt), .eq(is_eq));  // open: lt
  BarrelShifter #(.Bits(32)) lsl (.in(A), .shift(B[5:0]), .out(in_6));
  BarrelShifter #(.Bits(32), .direction("right")) lsr (.in(A), .shift(B[5:0]), .out(in_7));
  BarrelShifter #(.barrelShifterMode("arithmetic"), .Bits(32), .direction("right")) asr (
    .in(A), .shift(B[5:0]), .out(in_8));
  assign in_9 = ~B;  // Not not_1, 32 bits wide
  Multiplexer #(.Selector_Bits(4), .Bits(32)) multiplexer_1 (
    .sel(ALU_signals), .in_0(in_0), .in_1(in_1), .in_2(in_2), .in_3(in_3), .in_4(in_4), .in_5(in_6),
    .in_6(in_7), .in_7(in_8), .in_8(in_9), .in_9(in_10), .in_10(in_11), .in_11({32{1'b0}}),
    .in_12({32{1'b0}}), .in_13({32{1'b0}}), .in_14({32{1'b0}}), .in_15({32{1'b0}}), .out(aluResult));

  // Notes on the sheet:
  //   not
  //   and
  //   or
endmodule
